# Fritzing sketch Sketch (saved by Fritzing 0.9.3b)

parts:
  R1 = Resistor [tolerance=±5% resistance=220 package=THT]  # not connected
  Composant1 = The AirBoard
  DS1 = DS18B20 1-Wire Temperature Sensor [part_number=DS18B20]

nets:
  N1: Composant1.D3~/INT1, DS1.DQ
  3V3: Composant1.3V3, DS1.VDD
  GND: Composant1.GND, DS1.GND

custom parts:
  The AirBoard: The AirBoard is an ultra low-power Arduino-compatible prototyping platform for the Internet of Things, designed to explore, hack and deploy your killer idea in the field. It features a Bee socket for Bluetooth, WiFi, XBee, GSM/GPRS, SIGFOX and LoRa wireless modules, with Over-The-Air Programming support for Bluetooth and XBee. It comes with a 155mAh built-in rechargeable LiPo battery with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
